# Fritzing sketch LinkSensorProcess (saved by Fritzing 0.9.4)

parts:
  Bauteil1 = Arduino Pro Mini V2 (5V)
  U1 = WS2812 RGB LED strip
  C1 = Film/Foil Capacitor [capacitance=100nF voltage=35V package="27.5mm [THT, pp]"]
  R1 = Resistor [tolerance=±5% resistance=1M package="2010 [SMD]"]
  VCC1 = Battery block 9V

nets:
  VCC: Bauteil1.VCC, U1.VCC
  GND: Bauteil1.GND, U1.GND, VCC1.-
  N1: Bauteil1.RAW, VCC1.+
  N2: Bauteil1.D4, C1.+
  N3: Bauteil1.D3, R1.Pin_1
  N4: Bauteil1.D2, U1.DIN
  N5: C1.-, R1.Pin_0

custom parts:
  Arduino Pro Mini V2 (5V): Arduino Pro Mini V2 There are several different layouts for this board out there. This one is modeled after the Sparkfun 11113 board but a few of the pins have been moved around.
  WS2812 RGB LED strip: WS2812 strip
